// Logisim project alu.circ as structural Verilog: 1 circuit, main circuit main
module main (
  input  [15:0] X,
  input  [15:0] Y,
  input  [2:0] Switch,
  output Equal,
  output [15:0] Result,
  output [15:0] Result_2_a9898de3
);

  wire [3:0] bitselector_1_out;

  BitSelector #(.width(16), .group(4)) bitselector_1 (.in(Y), .out(bitselector_1_out), .sel(2'b00));
  Shifter #(.width(16)) shifter_1 (.in(X), .\dist (bitselector_1_out));  // open: out
  Shifter #(.width(16), .shift("lr")) shifter_2 (.in(X), .\dist (bitselector_1_out));  // open: out
  Adder #(.width(16)) adder_1 (.a(X), .b(Y));  // open: out, cin, cout
  // AND_Gate and_1 has open pins: in0=X, in1=Y, out=open
  assign Result = X | Y;  // OR_Gate or_1, 16 bits wide
  // XOR_Gate xor_1 is placed but not wired
  Comparator #(.width(16)) comparator_1 ();  // open: a, b, gt, eq, lt
  Multiplier #(.width(1)) multiplier_1 ();  // open: a, b, out, cin, cout

  // Other names for the same wires on the sheet: result_2[15:0] = Result_2_a9898de3; S[2:0] = Switch

  // Notes on the sheet:
  //   INPUTS to your circuit
  //   DON'T CHANGE THE LOCATIONS OF THE INPUTS AND OUTPUTS!
  //   OUTPUTS from your circuit
endmodule
